// Logisim project QuintenBallardALU.circ as structural Verilog: 12 circuits, main circuit Arch
module ALU (
  input  [7:0] A,
  input  [7:0] B,
  input  [2:0] opcode,
  output [7:0] O,
  output Cout
);

  wire fulladder_1_cout, fullsubtractor_1_cout;
  wire [3:0] formulti_1_oa, formulti_1_ob;
  wire [7:0] andgatemux_1_o, btoo_1_o, fulladder_1_o, fullsubtractor_1_o, multiplication_1_out_3,
       orgatemux_1_o, shiftright_1_o, xorgate_1_o;

  forMulti formulti_1 (.A(A), .B(B), .OA(formulti_1_oa), .OB(formulti_1_ob));
  BtoO btoo_1 (.B(B), .O(btoo_1_o));
  xorGate xorgate_1 (.A(A), .B(B), .O(xorgate_1_o));
  AndGateMux andgatemux_1 (.A(A), .B(B), .O(andgatemux_1_o));
  OrGateMux orgatemux_1 (.A(A), .B(B), .O(orgatemux_1_o));
  fullAdder fulladder_1 (.A(A), .B(B), .O(fulladder_1_o), .Cout(fulladder_1_cout));
  FullSubtractor fullsubtractor_1 (.A(A), .B(B), .O(fullsubtractor_1_o), .Cout(fullsubtractor_1_cout));
  shiftRight shiftright_1 (.B(B), .O(shiftright_1_o));
  multiplication multiplication_1 (.A(formulti_1_oa), .B(formulti_1_ob), .out_3(multiplication_1_out_3));
  Multiplexer #(.select(3), .width(8)) multiplexer_1 (
    .in0(btoo_1_o), .in1(xorgate_1_o), .in2(andgatemux_1_o), .in3(orgatemux_1_o), .in4(fulladder_1_o),
    .in5(fullsubtractor_1_o), .in6(shiftright_1_o), .in7(multiplication_1_out_3), .out(O), .sel(opcode));
  Multiplexer #(.select(3)) multiplexer_2 (
    .in4(fulladder_1_cout), .in5(fullsubtractor_1_cout), .out(Cout), .sel(opcode));  // open: in0, in1, in2, in3, in6, in7
endmodule

module Arch (
  input  [7:0] A,
  input  [7:0] B,
  input  [2:0] opcode,
  output [7:0] O,
  output out_5
);

  ALU alu_1 (.A(A), .B(B), .opcode(opcode), .O(O), .Cout(out_5));
endmodule

module AndGateMux (
  input  [7:0] A,
  input  [7:0] B,
  output [7:0] O
);

  and and_1 (O[0], A[0], B[0]);
  and and_2 (O[1], A[1], B[1]);
  and and_3 (O[2], A[2], B[2]);
  and and_4 (O[3], A[3], B[3]);
  and and_5 (O[4], A[4], B[4]);
  and and_6 (O[5], A[5], B[5]);
  and and_7 (O[6], A[6], B[6]);
  and and_8 (O[7], A[7], B[7]);
endmodule

module OrGateMux (
  input  [7:0] A,
  input  [7:0] B,
  output [7:0] O
);

  or or_1 (O[0], A[0], B[0]);
  or or_2 (O[1], A[1], B[1]);
  or or_3 (O[2], A[2], B[2]);
  or or_4 (O[3], A[3], B[3]);
  or or_5 (O[4], A[4], B[4]);
  or or_6 (O[5], A[5], B[5]);
  or or_7 (O[6], A[6], B[6]);
  or or_8 (O[7], A[7], B[7]);
endmodule

module xorGate (
  input  [7:0] A,
  input  [7:0] B,
  output [7:0] O
);

  xor xor_1 (O[0], A[0], B[0]);
  xor xor_2 (O[1], A[1], B[1]);
  xor xor_3 (O[2], A[2], B[2]);
  xor xor_4 (O[3], A[3], B[3]);
  xor xor_5 (O[4], A[4], B[4]);
  xor xor_6 (O[5], A[5], B[5]);
  xor xor_7 (O[6], A[6], B[6]);
  xor xor_8 (O[7], A[7], B[7]);
endmodule

module singlebitAdder (
  input  A,
  input  B,
  input  Cin,
  output O,
  output Cout
);

  wire and_1_out, and_2_out, xor_1_out;

  xor xor_1 (xor_1_out, A, B);
  and and_1 (and_1_out, Cin, xor_1_out);
  and and_2 (and_2_out, B, A);
  xor xor_2 (O, xor_1_out, Cin);
  or or_1 (Cout, and_1_out, and_2_out);
endmodule

module fullAdder (
  input  [7:0] A,
  input  [7:0] B,
  output [7:0] O,
  output Cout
);

  wire singlebitadder_1_cout, singlebitadder_2_cout, singlebitadder_3_cout, singlebitadder_4_cout,
       singlebitadder_5_cout, singlebitadder_6_cout, singlebitadder_7_cout;

  singlebitAdder singlebitadder_1 (.A(A[0]), .B(B[0]), .Cin(1'b0), .O(O[0]), .Cout(singlebitadder_1_cout));
  singlebitAdder singlebitadder_2 (
    .A(A[1]), .B(B[1]), .Cin(singlebitadder_1_cout), .O(O[1]), .Cout(singlebitadder_2_cout));
  singlebitAdder singlebitadder_3 (
    .A(A[2]), .B(B[2]), .Cin(singlebitadder_2_cout), .O(O[2]), .Cout(singlebitadder_3_cout));
  singlebitAdder singlebitadder_4 (
    .A(A[3]), .B(B[3]), .Cin(singlebitadder_3_cout), .O(O[3]), .Cout(singlebitadder_4_cout));
  singlebitAdder singlebitadder_5 (
    .A(A[4]), .B(B[4]), .Cin(singlebitadder_4_cout), .O(O[4]), .Cout(singlebitadder_5_cout));
  singlebitAdder singlebitadder_6 (
    .A(A[5]), .B(B[5]), .Cin(singlebitadder_5_cout), .O(O[5]), .Cout(singlebitadder_6_cout));
  singlebitAdder singlebitadder_7 (
    .A(A[6]), .B(B[6]), .Cin(singlebitadder_6_cout), .O(O[6]), .Cout(singlebitadder_7_cout));
  singlebitAdder singlebitadder_8 (.A(A[7]), .B(B[7]), .Cin(singlebitadder_7_cout), .O(O[7]), .Cout(Cout));
endmodule

module FullSubtractor (
  input  [7:0] A,
  input  [7:0] B,
  output [7:0] O,
  output Cout
);

  wire not_1_out, not_2_out, not_3_out, not_4_out, not_5_out, not_6_out, not_7_out, not_8_out,
       singlebitadder_1_cout, singlebitadder_2_cout, singlebitadder_3_cout, singlebitadder_4_cout,
       singlebitadder_5_cout, singlebitadder_6_cout, singlebitadder_7_cout;

  not not_1 (not_1_out, B[0]);
  not not_2 (not_2_out, B[1]);
  not not_3 (not_3_out, B[2]);
  not not_4 (not_4_out, B[3]);
  not not_5 (not_5_out, B[4]);
  not not_6 (not_6_out, B[5]);
  not not_7 (not_7_out, B[6]);
  not not_8 (not_8_out, B[7]);
  singlebitAdder singlebitadder_1 (.A(A[0]), .B(not_1_out), .Cin(1'b1), .O(O[0]), .Cout(singlebitadder_1_cout));
  singlebitAdder singlebitadder_2 (
    .A(A[1]), .B(not_2_out), .Cin(singlebitadder_1_cout), .O(O[1]), .Cout(singlebitadder_2_cout));
  singlebitAdder singlebitadder_3 (
    .A(A[2]), .B(not_3_out), .Cin(singlebitadder_2_cout), .O(O[2]), .Cout(singlebitadder_3_cout));
  singlebitAdder singlebitadder_4 (
    .A(A[3]), .B(not_4_out), .Cin(singlebitadder_3_cout), .O(O[3]), .Cout(singlebitadder_4_cout));
  singlebitAdder singlebitadder_5 (
    .A(A[4]), .B(not_5_out), .Cin(singlebitadder_4_cout), .O(O[4]), .Cout(singlebitadder_5_cout));
  singlebitAdder singlebitadder_6 (
    .A(A[5]), .B(not_6_out), .Cin(singlebitadder_5_cout), .O(O[5]), .Cout(singlebitadder_6_cout));
  singlebitAdder singlebitadder_7 (
    .A(A[6]), .B(not_7_out), .Cin(singlebitadder_6_cout), .O(O[6]), .Cout(singlebitadder_7_cout));
  singlebitAdder singlebitadder_8 (.A(A[7]), .B(not_8_out), .Cin(singlebitadder_7_cout), .O(O[7]), .Cout(Cout));
endmodule

module shiftRight (
  input  [7:0] B,
  output [7:0] O
);

  wire and_1_out, and_2_out, and_3_out, and_4_out, and_5_out, and_6_out, and_7_out, and_8_out, and_9_out,
       and_10_out, and_11_out, and_12_out, and_13_out, and_14_out, and_15_out, and_16_out, not_1_out,
       not_2_out, not_3_out, not_4_out, not_5_out, not_6_out, not_7_out, not_8_out;

  and and_1 (and_1_out, 1'b0, 1'b1);
  xor xor_1 (O[7], and_1_out, and_2_out);
  not not_1 (not_1_out, 1'b1);
  and and_2 (and_2_out, B[7], not_1_out);
  and and_3 (and_3_out, B[7], 1'b1);
  xor xor_2 (O[6], and_3_out, and_4_out);
  not not_2 (not_2_out, 1'b1);
  and and_4 (and_4_out, B[6], not_2_out);
  and and_5 (and_5_out, B[6], 1'b1);
  xor xor_3 (O[5], and_5_out, and_6_out);
  not not_3 (not_3_out, 1'b1);
  and and_6 (and_6_out, B[5], not_3_out);
  and and_7 (and_7_out, B[5], 1'b1);
  not not_4 (not_4_out, 1'b1);
  and and_8 (and_8_out, B[4], not_4_out);
  xor xor_4 (O[4], and_7_out, and_8_out);
  and and_9 (and_9_out, B[4], 1'b1);
  not not_5 (not_5_out, 1'b1);
  and and_10 (and_10_out, B[3], not_5_out);
  xor xor_5 (O[3], and_9_out, and_10_out);
  and and_11 (and_11_out, B[3], 1'b1);
  and and_12 (and_12_out, B[2], not_6_out);
  xor xor_6 (O[2], and_11_out, and_12_out);
  not not_6 (not_6_out, 1'b1);
  and and_13 (and_13_out, B[2], 1'b1);
  xor xor_7 (O[1], and_13_out, and_14_out);
  not not_7 (not_7_out, 1'b1);
  and and_14 (and_14_out, B[1], not_7_out);
  and and_15 (and_15_out, B[1], 1'b1);
  and and_16 (and_16_out, B[0], not_8_out);
  xor xor_8 (O[0], and_15_out, and_16_out);
  not not_8 (not_8_out, 1'b1);
endmodule

module BtoO (
  input  [7:0] B,
  output [7:0] O
);


  assign O = B;
endmodule

module multiplication (
  input  [3:0] A,
  input  [3:0] B,
  output [7:0] out_3
);

  wire and_1_out, and_2_out, and_3_out, and_4_out, and_6_out, and_7_out, and_8_out, and_9_out, and_10_out,
       and_11_out, and_12_out, and_13_out, and_14_out, and_15_out, and_16_out, singlebitadder_1_cout,
       singlebitadder_1_o, singlebitadder_2_cout, singlebitadder_2_o, singlebitadder_3_cout,
       singlebitadder_4_cout, singlebitadder_4_o, singlebitadder_5_cout, singlebitadder_5_o,
       singlebitadder_6_cout, singlebitadder_7_cout, singlebitadder_7_o, singlebitadder_8_cout,
       singlebitadder_8_o, singlebitadder_9_cout, singlebitadder_10_cout, singlebitadder_11_cout;

  and and_1 (and_1_out, A[2], B[0]);
  and and_2 (and_2_out, A[3], B[0]);
  and and_3 (and_3_out, A[3], B[1]);
  and and_4 (and_4_out, A[2], B[2]);
  and and_5 (out_3[0], A[0], B[0]);
  and and_6 (and_6_out, A[1], B[0]);
  and and_7 (and_7_out, A[0], B[1]);
  and and_8 (and_8_out, A[1], B[1]);
  and and_9 (and_9_out, A[2], B[1]);
  and and_10 (and_10_out, A[3], B[2]);
  and and_11 (and_11_out, A[1], B[2]);
  and and_12 (and_12_out, A[0], B[2]);
  singlebitAdder singlebitadder_1 (
    .A(and_2_out), .B(and_9_out), .Cin(singlebitadder_4_cout), .O(singlebitadder_1_o),
    .Cout(singlebitadder_1_cout));
  singlebitAdder singlebitadder_2 (
    .A(singlebitadder_1_cout), .B(and_3_out), .Cin(1'b0), .O(singlebitadder_2_o), .Cout(singlebitadder_2_cout));
  singlebitAdder singlebitadder_3 (
    .A(and_6_out), .B(and_7_out), .Cin(1'b0), .O(out_3[1]), .Cout(singlebitadder_3_cout));
  singlebitAdder singlebitadder_4 (
    .A(and_1_out), .B(and_8_out), .Cin(singlebitadder_3_cout), .O(singlebitadder_4_o),
    .Cout(singlebitadder_4_cout));
  and and_13 (and_13_out, A[3], B[3]);
  singlebitAdder singlebitadder_5 (
    .A(singlebitadder_2_cout), .B(and_10_out), .Cin(singlebitadder_8_cout), .O(singlebitadder_5_o),
    .Cout(singlebitadder_5_cout));
  and and_14 (and_14_out, A[0], B[3]);
  singlebitAdder singlebitadder_6 (
    .A(singlebitadder_4_o), .B(and_12_out), .Cin(1'b0), .O(out_3[2]), .Cout(singlebitadder_6_cout));
  singlebitAdder singlebitadder_7 (
    .A(singlebitadder_1_o), .B(and_11_out), .Cin(singlebitadder_6_cout), .O(singlebitadder_7_o),
    .Cout(singlebitadder_7_cout));
  singlebitAdder singlebitadder_8 (
    .A(singlebitadder_2_o), .B(and_4_out), .Cin(singlebitadder_7_cout), .O(singlebitadder_8_o),
    .Cout(singlebitadder_8_cout));
  and and_15 (and_15_out, A[1], B[3]);
  and and_16 (and_16_out, A[2], B[3]);
  singlebitAdder singlebitadder_9 (
    .A(singlebitadder_7_o), .B(and_14_out), .Cin(1'b0), .O(out_3[3]), .Cout(singlebitadder_9_cout));
  singlebitAdder singlebitadder_10 (
    .A(singlebitadder_8_o), .B(and_15_out), .Cin(singlebitadder_9_cout), .O(out_3[4]),
    .Cout(singlebitadder_10_cout));
  singlebitAdder singlebitadder_11 (
    .A(singlebitadder_5_o), .B(and_16_out), .Cin(singlebitadder_10_cout), .O(out_3[5]),
    .Cout(singlebitadder_11_cout));
  singlebitAdder singlebitadder_12 (
    .A(singlebitadder_5_cout), .B(and_13_out), .Cin(singlebitadder_11_cout), .O(out_3[6]), .Cout(out_3[7]));
endmodule

module forMulti (
  input  [7:0] A,
  input  [7:0] B,
  output [3:0] OA,
  output [3:0] OB
);


  assign OA = A[3:0];
  assign OB = B[3:0];
endmodule
